// Logisim project Ori Cpu.circ as structural Verilog: 1 circuit, main circuit main
module main (
  output [7:0] out_1,
  output [1:0] Target,
  output [7:0] RegData1,
  output [7:0] out_4,
  output [7:0] ByteReader,
  output [7:0] out_6,
  output [7:0] RegData2,
  output [7:0] out_8,
  output [1:0] out_9,
  output [7:0] out_10
);

  wire and_1_out, and_2_out, and_3_out, and_4_out, and_5_out, and_6_out, and_7_out, cl_out, decoder_1_out0,
       decoder_1_out1, decoder_1_out2, decoder_1_out3, Memclock_out, multiplexer_1_out, multiplexer_2_out,
       multiplexer_3_out, multiplexer_4_out;
  wire [1:0] multiplexer_5_out;
  wire [7:0] adder_1_out, adder_3_out, bit_extender_1_out, MemoryInput_dout, multiplexer_7_out,
       multiplexer_9_out, not_1_out, pc_q, reg1_q, reg2_q, reg3_q, reg4_q, undriven;

  Clock #(.highDuration(3)) cl (.out(cl_out));
  Register pc (.D(adder_1_out), .clk(cl_out), .Q(pc_q));  // open: en, clr
  Adder adder_1 (.a(pc_q), .b(8'h1), .out(adder_1_out));  // open: cin, cout
  RAM memory (.addr(pc_q), .we(1'b0), .oe(1'b1), .clk(cl_out), .din(undriven), .dout(ByteReader));
  assign not_1_out = ~pc_q;  // NOT_Gate not_1, 8 bits wide
  and and_1 (and_1_out, not_1_out[0], not_1_out[1], not_1_out[2], not_1_out[3]);
  and and_2 (and_2_out, not_1_out[4], not_1_out[5], not_1_out[6], not_1_out[7]);
  and and_3 (and_3_out, and_1_out, and_2_out);
  Decoder #(.select(2)) decoder_1 (
    .out0(decoder_1_out0), .out1(decoder_1_out1), .out2(decoder_1_out2), .out3(decoder_1_out3),
    .sel(ByteReader[1:0]));  // open: en
  Multiplexer #(.select(2)) multiplexer_1 (
    .in0(1'b0), .in1(1'b0), .in2(1'b0), .in3(1'b1), .out(multiplexer_1_out), .sel(ByteReader[7:6]));
  Multiplexer #(.select(2)) multiplexer_2 (
    .in0(1'b0), .in1(1'b0), .in2(1'b1), .in3(1'b0), .out(multiplexer_2_out), .sel(ByteReader[7:6]));
  Multiplexer #(.select(2)) multiplexer_3 (
    .in0(1'b0), .in1(1'b0), .in2(1'b0), .in3(1'b1), .out(multiplexer_3_out), .sel(ByteReader[7:6]));
  Multiplexer #(.select(2)) multiplexer_4 (
    .in0(1'b0), .in1(1'b1), .in2(1'b1), .in3(1'b1), .out(multiplexer_4_out), .sel(ByteReader[7:6]));
  and and_4 (and_4_out, decoder_1_out0, multiplexer_4_out);
  and and_5 (and_5_out, decoder_1_out1, multiplexer_4_out);
  and and_6 (and_6_out, decoder_1_out2, multiplexer_4_out);
  and and_7 (and_7_out, decoder_1_out3, multiplexer_4_out);
  assign bit_extender_1_out = {{6{multiplexer_5_out[1]}}, multiplexer_5_out};  // Bit_Extender bit_extender_1
  Multiplexer #(.width(2)) multiplexer_5 (
    .in0(2'b00), .in1(ByteReader[5:4]), .out(multiplexer_5_out), .sel(multiplexer_3_out));
  Register reg1 (.D(out_6), .en(and_4_out), .clk(cl_out), .Q(reg1_q), .clr(and_3_out));
  Register #(.trigger("falling")) reg2 (.D(out_6), .en(and_5_out), .clk(cl_out), .Q(reg2_q), .clr(and_3_out));
  Register reg3 (.D(out_6), .en(and_6_out), .clk(cl_out), .Q(reg3_q), .clr(and_3_out));
  Register reg4 (.D(out_6), .en(and_7_out), .clk(cl_out), .Q(reg4_q), .clr(and_3_out));
  Adder adder_2 (.a(out_8), .b(bit_extender_1_out), .out(out_10));  // open: cin, cout
  Hex_Digit_Display hex_digit_display_1 (.value(out_6[7:4]));  // open: dp
  Hex_Digit_Display hex_digit_display_2 (.value(out_6[3:0]));  // open: dp
  Multiplexer #(.select(2), .width(8)) multiplexer_6 (
    .in0(reg1_q), .in1(reg2_q), .in2(reg3_q), .in3(reg4_q), .out(out_8), .sel(ByteReader[3:2]));
  Multiplexer #(.select(2), .width(8)) multiplexer_7 (
    .in0(reg1_q), .in1(reg2_q), .in2(reg3_q), .in3(reg4_q), .out(multiplexer_7_out), .sel(ByteReader[5:4]));
  Multiplexer #(.width(8)) multiplexer_8 (
    .in0(multiplexer_7_out), .in1(bit_extender_1_out), .out(RegData2), .sel(multiplexer_3_out));
  Adder adder_3 (.a(out_8), .b(RegData2), .out(adder_3_out));  // open: cin, cout
  assign out_4 = out_8 & RegData2;  // AND_Gate and_8, 8 bits wide
  Multiplexer #(.width(8)) multiplexer_9 (
    .in0(adder_3_out), .in1(out_4), .out(multiplexer_9_out), .sel(multiplexer_2_out));
  Multiplexer #(.width(8)) multiplexer_10 (.in0(multiplexer_9_out), .in1(out_10), .out(out_1), .sel(multiplexer_1_out));
  Clock Memclock (.out(Memclock_out));
  RAM MemoryInput (.addr(out_1), .we(1'b0), .oe(1'b1), .clk(Memclock_out), .dout(MemoryInput_dout));  // open: din
  Multiplexer #(.width(8)) multiplexer_11 (.in0(out_1), .in1(MemoryInput_dout), .out(out_6), .sel(multiplexer_1_out));

  assign out_9 = ByteReader[5:4];
  assign RegData1 = out_8;
  assign Target = ByteReader[1:0];

  // Notes on the sheet:
  //   Pc Adder 
  //   Kush Parmar
  //   Write Enable
  //   OutPut Enable
  //   I pledge my honor that I have abided by the Stevens Honor System
  //   Instruction Memory
  //   WriteReg
  //   RegWrite
  //   Operation
  //   AluSrc
  //   Immediate offset 
  //   ReadData2
  //   ReadData1
  //   Add Operation
  //   And operation
  //   AluOut
  //   MemToReg
  //   Data Memory
  //   RegWrite
endmodule
